// Logisim project control.circ as structural Verilog: 1 circuit, main circuit main
module main (
  input  Start,
  input  lastbit,
  input  finish,
  input  clock,
  output resetcounter,
  output sp,
  output SPmiler,
  output increase,
  output shift,
  output add,
  output carry,
  output lastbit0_1,
  output resetcarry
);

  wire and_2_out, and_3_out, and_4_out, and_5_out, and_6_out, and_7_out, and_8_out, and_9_out, and_10_out,
       not_1_out, not_2_out, not_3_out, not_4_out, not_5_out, not_6_out, not_7_out, not_8_out, not_9_out,
       not_10_out, not_11_out, not_12_out, not_13_out, not_14_out, not_15_out, not_16_out, not_17_out,
       not_18_out, not_19_out, not_20_out, not_21_out, not_22_out, not_23_out, not_24_out, not_25_out,
       not_26_out, not_27_out, not_28_out, S1_out;
  wire [2:0] or_4_out, register_1_q;

  // AND_Gate and_1 is placed but not wired
  Register #(.width(3)) register_1 (.D(or_4_out), .en(1'b1), .Q(register_1_q), .clk(clock));  // open: clr
  not not_1 (not_1_out, register_1_q[0]);
  not not_2 (not_2_out, register_1_q[1]);
  not not_3 (not_3_out, register_1_q[2]);
  not not_4 (not_4_out, register_1_q[2]);
  not not_5 (not_5_out, register_1_q[0]);
  not not_6 (not_6_out, lastbit);
  not not_7 (not_7_out, register_1_q[2]);
  not not_8 (not_8_out, register_1_q[1]);
  not not_9 (not_9_out, register_1_q[0]);
  and and_2 (and_2_out, Start, not_1_out, not_2_out, not_3_out);
  not not_10 (not_10_out, register_1_q[0]);
  not not_11 (not_11_out, register_1_q[1]);
  not not_12 (not_12_out, register_1_q[1]);
  not not_13 (not_13_out, register_1_q[2]);
  not not_14 (not_14_out, register_1_q[0]);
  and and_3 (and_3_out, not_4_out, register_1_q[1], not_5_out, not_6_out);
  and and_4 (and_4_out, not_7_out, register_1_q[1], register_1_q[0]);
  and and_5 (and_5_out, register_1_q[2], not_8_out, not_9_out, finish);
  and and_6 (and_6_out, not_10_out, not_11_out, register_1_q[2]);
  and and_7 (and_7_out, register_1_q[0], not_12_out, not_13_out);
  and and_8 (and_8_out, not_13_out, register_1_q[1], not_14_out, lastbit);
  or or_1 (or_4_out[2], and_3_out, and_4_out, and_5_out);
  or or_2 (or_4_out[1], and_6_out, and_7_out, and_8_out);
  not not_15 (not_15_out, register_1_q[2]);
  not not_16 (not_16_out, register_1_q[0]);
  and and_9 (and_9_out, not_15_out, register_1_q[1], not_16_out, lastbit);
  not not_17 (not_17_out, register_1_q[1]);
  not not_18 (not_18_out, register_1_q[0]);
  not not_19 (not_19_out, register_1_q[2]);
  not not_20 (not_20_out, register_1_q[1]);
  not not_21 (not_21_out, register_1_q[0]);
  not not_22 (not_22_out, register_1_q[2]);
  not not_23 (not_23_out, register_1_q[1]);
  not not_24 (not_24_out, register_1_q[1]);
  not not_25 (not_25_out, register_1_q[0]);
  not not_26 (not_26_out, register_1_q[2]);
  not not_27 (not_27_out, register_1_q[2]);
  not not_28 (not_28_out, register_1_q[0]);
  and and_10 (and_10_out, register_1_q[2], finish, not_17_out, not_18_out);
  and S0 (resetcounter, not_19_out, not_20_out, not_21_out);
  and S1 (S1_out, not_22_out, not_23_out, register_1_q[0]);
  and S4 (increase, register_1_q[2], not_24_out, not_25_out);
  and S3 (add, not_26_out, register_1_q[1], register_1_q[0]);
  and S2 (resetcarry, not_27_out, register_1_q[1], not_28_out);
  or or_3 (SPmiler, S1_out, increase);
  or or_4 (or_4_out[0], and_2_out, and_9_out, and_10_out);
  or or_5 (sp, S1_out, increase, add);
  // AND_Gate and_11 is placed but not wired

  assign carry = add;
  assign lastbit0_1 = add;
  assign shift = increase;
endmodule
