// Logisim project datapath.circ as structural Verilog: 4 circuits, main circuit main
module main (
  input  [31:0] Multiplicand,
  input  Clock,
  input  LastBit0_1,
  input  carry,
  input  resetcarry,
  input  add,
  input  shift,
  input  SP,
  input  [31:0] Multiplier,
  input  SMlier,
  input  increase,
  input  resetcounter,
  output [31:0] HIResult,
  output lastbit,
  output [31:0] LOresult,
  output finish
);

  wire n32_bit_adder_1_carryout, register_3_q, xnor_1_out, xnor_2_out, xnor_3_out, xnor_4_out, xnor_5_out,
       xnor_6_out;
  wire [5:0] counter_1_q;
  wire [31:0] multiplexer_1_out, multiplexer_2_out, multiplexer_3_out, multiplexer_4_out,
       n1_bit_right_shifter_1_hi32out, n1_bit_right_shifter_1_lo32out, n32_bit_adder_1_addresult;

  Multiplexer #(.width(32), .enable("false")) multiplexer_1 (
    .in0({32{1'b0}}), .in1(multiplexer_4_out), .out(multiplexer_1_out), .sel(add));
  Multiplexer #(.width(32), .enable("false")) multiplexer_2 (
    .in0(Multiplier), .in1(n1_bit_right_shifter_1_lo32out), .out(multiplexer_2_out), .sel(shift));
  Multiplexer #(.width(32), .enable("false")) multiplexer_3 (
    .in0(multiplexer_1_out), .in1(n1_bit_right_shifter_1_hi32out), .out(multiplexer_3_out), .sel(shift));
  Register #(.width(32)) register_1 (
    .D(multiplexer_2_out), .en(SMlier), .Q({LOresult[31:1], lastbit}), .clk(Clock));  // open: clr
  _32_bit_adder u_32_bit_adder_1 (
    .A(Multiplicand), .B(HIResult), .carryout(n32_bit_adder_1_carryout), .addResult(n32_bit_adder_1_addresult));
  Register #(.width(32)) register_2 (.D(multiplexer_3_out), .en(SP), .Q(HIResult), .clk(Clock));  // open: clr
  Counter #(.width(6), .max('h3f)) counter_1 (
    .D({6{1'b0}}), .Q(counter_1_q), .clk(increase), .clr(resetcounter));  // open: load, count, carry
  Multiplexer #(.width(32), .enable("false")) multiplexer_4 (
    .in0(HIResult), .in1(n32_bit_adder_1_addresult), .out(multiplexer_4_out), .sel(LastBit0_1));
  Register #(.width(1)) register_3 (
    .D(n32_bit_adder_1_carryout), .en(carry), .Q(register_3_q), .clk(Clock), .clr(resetcarry));
  xnor xnor_1 (xnor_1_out, 1'b0, counter_1_q[0]);
  xnor xnor_2 (xnor_2_out, 1'b0, counter_1_q[1]);
  xnor xnor_3 (xnor_3_out, 1'b0, counter_1_q[2]);
  xnor xnor_4 (xnor_4_out, 1'b0, counter_1_q[3]);
  xnor xnor_5 (xnor_5_out, 1'b0, counter_1_q[4]);
  xnor xnor_6 (xnor_6_out, 1'b1, counter_1_q[5]);
  _1_bit_right_Shifter u_1_bit_right_shifter_1 (
    .HI32(HIResult), .carryOut(register_3_q), .LO32({LOresult[31:1], lastbit}),
    .HI32out(n1_bit_right_shifter_1_hi32out), .LO32out(n1_bit_right_shifter_1_lo32out));
  and and_1 (finish, xnor_1_out, xnor_2_out, xnor_3_out, xnor_4_out, xnor_5_out, xnor_6_out);

  assign LOresult[0] = lastbit;
endmodule

// right shifter
module _1_bit_right_Shifter (
  input  [31:0] HI32,
  input  carryOut,
  input  [31:0] LO32,
  output [31:0] HI32out,
  output [31:0] LO32out
);


  assign HI32out = {carryOut, HI32[31:1]};
  assign LO32out = {HI32[0], LO32[31:1]};
endmodule

// 32 bit Adder
module _32_bit_adder (
  input  [31:0] A,
  input  [31:0] B,
  output carryout,
  output [31:0] addResult
);

  wire n1_bit_adder_1_c_out, n1_bit_adder_2_c_out, n1_bit_adder_3_c_out, n1_bit_adder_4_c_out,
       n1_bit_adder_5_c_out, n1_bit_adder_6_c_out, n1_bit_adder_7_c_out, n1_bit_adder_8_c_out,
       n1_bit_adder_9_c_out, n1_bit_adder_10_c_out, n1_bit_adder_11_c_out, n1_bit_adder_12_c_out,
       n1_bit_adder_13_c_out, n1_bit_adder_14_c_out, n1_bit_adder_15_c_out, n1_bit_adder_16_c_out,
       n1_bit_adder_17_c_out, n1_bit_adder_18_c_out, n1_bit_adder_19_c_out, n1_bit_adder_20_c_out,
       n1_bit_adder_21_c_out, n1_bit_adder_22_c_out, n1_bit_adder_23_c_out, n1_bit_adder_24_c_out,
       n1_bit_adder_25_c_out, n1_bit_adder_26_c_out, n1_bit_adder_27_c_out, n1_bit_adder_28_c_out,
       n1_bit_adder_29_c_out, n1_bit_adder_30_c_out, n1_bit_adder_31_c_out;

  _1_bit_adder u_1_bit_adder_1 (.a(A[0]), .b(B[0]), .c_in(1'b0), .sum(addResult[0]), .c_out(n1_bit_adder_1_c_out));
  _1_bit_adder u_1_bit_adder_2 (
    .a(A[2]), .b(B[2]), .c_in(n1_bit_adder_3_c_out), .sum(addResult[2]), .c_out(n1_bit_adder_2_c_out));
  _1_bit_adder u_1_bit_adder_3 (
    .a(A[1]), .b(B[1]), .c_in(n1_bit_adder_1_c_out), .sum(addResult[1]), .c_out(n1_bit_adder_3_c_out));
  _1_bit_adder u_1_bit_adder_4 (
    .a(A[3]), .b(B[3]), .c_in(n1_bit_adder_2_c_out), .sum(addResult[3]), .c_out(n1_bit_adder_4_c_out));
  _1_bit_adder u_1_bit_adder_5 (
    .a(A[4]), .b(B[4]), .c_in(n1_bit_adder_4_c_out), .sum(addResult[4]), .c_out(n1_bit_adder_5_c_out));
  _1_bit_adder u_1_bit_adder_6 (
    .a(A[5]), .b(B[5]), .c_in(n1_bit_adder_5_c_out), .sum(addResult[5]), .c_out(n1_bit_adder_6_c_out));
  _1_bit_adder u_1_bit_adder_7 (
    .a(A[6]), .b(B[6]), .c_in(n1_bit_adder_6_c_out), .sum(addResult[6]), .c_out(n1_bit_adder_7_c_out));
  _1_bit_adder u_1_bit_adder_8 (
    .a(A[7]), .b(B[7]), .c_in(n1_bit_adder_7_c_out), .sum(addResult[7]), .c_out(n1_bit_adder_8_c_out));
  _1_bit_adder u_1_bit_adder_9 (
    .a(A[8]), .b(B[8]), .c_in(n1_bit_adder_8_c_out), .sum(addResult[8]), .c_out(n1_bit_adder_9_c_out));
  _1_bit_adder u_1_bit_adder_10 (
    .a(A[9]), .b(B[9]), .c_in(n1_bit_adder_9_c_out), .sum(addResult[9]), .c_out(n1_bit_adder_10_c_out));
  _1_bit_adder u_1_bit_adder_11 (
    .a(A[10]), .b(B[10]), .c_in(n1_bit_adder_10_c_out), .sum(addResult[10]), .c_out(n1_bit_adder_11_c_out));
  _1_bit_adder u_1_bit_adder_12 (
    .a(A[11]), .b(B[11]), .c_in(n1_bit_adder_11_c_out), .sum(addResult[11]), .c_out(n1_bit_adder_12_c_out));
  _1_bit_adder u_1_bit_adder_13 (
    .a(A[12]), .b(B[12]), .c_in(n1_bit_adder_12_c_out), .sum(addResult[12]), .c_out(n1_bit_adder_13_c_out));
  _1_bit_adder u_1_bit_adder_14 (
    .a(A[13]), .b(B[13]), .c_in(n1_bit_adder_13_c_out), .sum(addResult[13]), .c_out(n1_bit_adder_14_c_out));
  _1_bit_adder u_1_bit_adder_15 (
    .a(A[14]), .b(B[14]), .c_in(n1_bit_adder_14_c_out), .sum(addResult[14]), .c_out(n1_bit_adder_15_c_out));
  _1_bit_adder u_1_bit_adder_16 (
    .a(A[15]), .b(B[15]), .c_in(n1_bit_adder_15_c_out), .sum(addResult[15]), .c_out(n1_bit_adder_16_c_out));
  _1_bit_adder u_1_bit_adder_17 (
    .a(A[16]), .b(B[16]), .c_in(n1_bit_adder_16_c_out), .sum(addResult[16]), .c_out(n1_bit_adder_17_c_out));
  _1_bit_adder u_1_bit_adder_18 (
    .a(A[17]), .b(B[17]), .c_in(n1_bit_adder_17_c_out), .sum(addResult[17]), .c_out(n1_bit_adder_18_c_out));
  _1_bit_adder u_1_bit_adder_19 (
    .a(A[18]), .b(B[18]), .c_in(n1_bit_adder_18_c_out), .sum(addResult[18]), .c_out(n1_bit_adder_19_c_out));
  _1_bit_adder u_1_bit_adder_20 (
    .a(A[19]), .b(B[19]), .c_in(n1_bit_adder_19_c_out), .sum(addResult[19]), .c_out(n1_bit_adder_20_c_out));
  _1_bit_adder u_1_bit_adder_21 (
    .a(A[20]), .b(B[20]), .c_in(n1_bit_adder_20_c_out), .sum(addResult[20]), .c_out(n1_bit_adder_21_c_out));
  _1_bit_adder u_1_bit_adder_22 (
    .a(A[21]), .b(B[21]), .c_in(n1_bit_adder_21_c_out), .sum(addResult[21]), .c_out(n1_bit_adder_22_c_out));
  _1_bit_adder u_1_bit_adder_23 (
    .a(A[22]), .b(B[22]), .c_in(n1_bit_adder_22_c_out), .sum(addResult[22]), .c_out(n1_bit_adder_23_c_out));
  _1_bit_adder u_1_bit_adder_24 (
    .a(A[23]), .b(B[23]), .c_in(n1_bit_adder_23_c_out), .sum(addResult[23]), .c_out(n1_bit_adder_24_c_out));
  _1_bit_adder u_1_bit_adder_25 (
    .a(A[24]), .b(B[24]), .c_in(n1_bit_adder_24_c_out), .sum(addResult[24]), .c_out(n1_bit_adder_25_c_out));
  _1_bit_adder u_1_bit_adder_26 (
    .a(A[25]), .b(B[25]), .c_in(n1_bit_adder_25_c_out), .sum(addResult[25]), .c_out(n1_bit_adder_26_c_out));
  _1_bit_adder u_1_bit_adder_27 (
    .a(A[26]), .b(B[26]), .c_in(n1_bit_adder_26_c_out), .sum(addResult[26]), .c_out(n1_bit_adder_27_c_out));
  _1_bit_adder u_1_bit_adder_28 (
    .a(A[27]), .b(B[27]), .c_in(n1_bit_adder_27_c_out), .sum(addResult[27]), .c_out(n1_bit_adder_28_c_out));
  _1_bit_adder u_1_bit_adder_29 (
    .a(A[28]), .b(B[28]), .c_in(n1_bit_adder_28_c_out), .sum(addResult[28]), .c_out(n1_bit_adder_29_c_out));
  _1_bit_adder u_1_bit_adder_30 (
    .a(A[29]), .b(B[29]), .c_in(n1_bit_adder_29_c_out), .sum(addResult[29]), .c_out(n1_bit_adder_30_c_out));
  _1_bit_adder u_1_bit_adder_31 (
    .a(A[30]), .b(B[30]), .c_in(n1_bit_adder_30_c_out), .sum(addResult[30]), .c_out(n1_bit_adder_31_c_out));
  _1_bit_adder u_1_bit_adder_32 (
    .a(A[31]), .b(B[31]), .c_in(n1_bit_adder_31_c_out), .sum(addResult[31]), .c_out(carryout));
endmodule

module _1_bit_adder (
  input  a,
  input  b,
  input  c_in,
  output sum,
  output c_out
);

  wire and_1_out, and_2_out, xor_1_out;

  xor xor_1 (xor_1_out, a, b);
  xor xor_2 (sum, xor_1_out, c_in);
  and and_1 (and_1_out, c_in, xor_1_out);
  and and_2 (and_2_out, a, b);
  or or_1 (c_out, and_1_out, and_2_out);
endmodule
