// Logisim project mult32.circ as structural Verilog: 1 circuit, main circuit main
module main (
  input  [31:0] A,
  input  [31:0] B,
  output [31:0] HIResult,
  output [31:0] LOResult
);

  wire clock_1_out, main_1_add, main_1_carry, main_1_increase, main_1_lastbit0_1, main_1_resetcarry,
       main_1_resetcounter, main_1_shift, main_1_sp, main_1_spmiler, main_2_finish, main_2_lastbit, START_out;

  Button START (.out(START_out));
  Clock clock_1 (.out(clock_1_out));
  control_main main_1 (
    .Start(START_out), .lastbit(main_2_lastbit), .finish(main_2_finish), .clock(clock_1_out),
    .resetcounter(main_1_resetcounter), .sp(main_1_sp), .SPmiler(main_1_spmiler), .increase(main_1_increase),
    .shift(main_1_shift), .add(main_1_add), .carry(main_1_carry), .lastbit0_1(main_1_lastbit0_1),
    .resetcarry(main_1_resetcarry));
  datapath_main main_2 (
    .Multiplicand(A), .Clock(clock_1_out), .LastBit0_1(main_1_lastbit0_1), .carry(main_1_carry),
    .resetcarry(main_1_resetcarry), .add(main_1_add), .shift(main_1_shift), .SP(main_1_sp), .Multiplier(B),
    .lastbit(main_2_lastbit), .SMlier(main_1_spmiler), .increase(main_1_increase),
    .resetcounter(main_1_resetcounter), .HIResult(HIResult), .LOresult(LOResult), .finish(main_2_finish));
endmodule
